// Logisim project trabalhoFinal1.circ as structural Verilog: 9 circuits, main circuit Seletor
module main (
  input  [2:0] sel,
  input  [3:0] A,
  input  [3:0] B,
  output [4:0] S
);

  menu_logico menu_logico_1 (.sel(sel), .A(A), .B(B), .S(S));
endmodule

module menu_logico (
  input  [2:0] sel,
  input  [3:0] A,
  input  [3:0] B,
  output [4:0] S
);

  wire seletor_1_s1, seletor_1_s2;
  wire [4:0] adder_4bits_1_out_4, subtractor_4bits_1_out_4;

  Seletor seletor_1 (.A(sel), .s1(seletor_1_s1), .s2(seletor_1_s2));  // open: s3, s4, s5, s6, s7, s8
  adder_4bits adder_4bits_1 (.sig(seletor_1_s1), .A(A), .B(B), .out_4(adder_4bits_1_out_4));
  subtractor_4bits subtractor_4bits_1 (.sig(seletor_1_s2), .A(A), .B(B), .out_4(subtractor_4bits_1_out_4));
  or_vet or_vet_1 (.A(adder_4bits_1_out_4), .B(subtractor_4bits_1_out_4), .S(S));
endmodule

module Seletor (
  input  [2:0] A,
  output s1,
  output s2,
  output s3,
  output s4,
  output s5,
  output s6,
  output s7,
  output s8
);

  wire not_1_out, not_2_out, not_3_out;

  not not_1 (not_1_out, A[2]);
  not not_2 (not_2_out, A[1]);
  not not_3 (not_3_out, A[0]);
  and and_1 (s1, not_1_out, not_2_out, not_3_out);
  and and_2 (s2, not_1_out, not_2_out, A[0]);
  and and_3 (s3, not_1_out, A[1], not_3_out);
  and and_4 (s4, not_1_out, A[1], A[0]);
  and and_5 (s5, A[2], not_2_out, not_3_out);
  and and_6 (s6, A[2], not_2_out, A[0]);
  and and_7 (s7, A[2], A[1], not_3_out);
  and and_8 (s8, A[2], A[1], A[0]);
endmodule

module adder_4bits (
  input  sig,
  input  [3:0] A,
  input  [3:0] B,
  output [4:0] out_4
);

  wire A0_out, A1_out, A2_out, A3_out, B0_out, B1_out, B2_out, B3_out, full_adder_2_cout, full_adder_3_cout,
       full_adder_4_cout;

  and B3 (B3_out, A[3], sig);
  and B2 (B2_out, A[2], sig);
  full_adder full_adder_1 (.A(B3_out), .B(A3_out), .Cin(full_adder_2_cout), .S(out_4[3]), .Cout(out_4[4]));
  and B1 (B1_out, A[1], sig);
  and B0 (B0_out, A[0], sig);
  full_adder full_adder_2 (.A(B2_out), .B(A2_out), .Cin(full_adder_3_cout), .S(out_4[2]), .Cout(full_adder_2_cout));
  and A3 (A3_out, B[3], sig);
  and A2 (A2_out, B[2], sig);
  full_adder full_adder_3 (.A(B1_out), .B(A1_out), .Cin(full_adder_4_cout), .S(out_4[1]), .Cout(full_adder_3_cout));
  and A1 (A1_out, B[1], sig);
  and A0 (A0_out, B[0], sig);
  full_adder full_adder_4 (.A(B0_out), .B(A0_out), .Cin(1'b0), .S(out_4[0]), .Cout(full_adder_4_cout));
endmodule

module subtractor_4bits (
  input  sig,
  input  [3:0] A,
  input  [3:0] B,
  output [4:0] out_4
);

  wire A0_out, A1_out, A2_out, A3_out, B0_out, B1_out, B2_out, B3_out, full_subtractor_2_cout,
       full_subtractor_3_cout, full_subtractor_4_cout;

  and B3 (B3_out, A[3], sig);
  and B2 (B2_out, A[2], sig);
  full_subtractor full_subtractor_1 (
    .A(B3_out), .B(A3_out), .Cin(full_subtractor_2_cout), .S(out_4[3]), .Cout(out_4[4]));
  and B1 (B1_out, A[1], sig);
  and B0 (B0_out, A[0], sig);
  full_subtractor full_subtractor_2 (
    .A(B2_out), .B(A2_out), .Cin(full_subtractor_3_cout), .S(out_4[2]), .Cout(full_subtractor_2_cout));
  and A3 (A3_out, B[3], sig);
  and A2 (A2_out, B[2], sig);
  full_subtractor full_subtractor_3 (
    .A(B1_out), .B(A1_out), .Cin(full_subtractor_4_cout), .S(out_4[1]), .Cout(full_subtractor_3_cout));
  and A1 (A1_out, B[1], sig);
  and A0 (A0_out, B[0], sig);
  full_subtractor full_subtractor_4 (.A(B0_out), .B(A0_out), .Cin(1'b0), .S(out_4[0]), .Cout(full_subtractor_4_cout));
endmodule

module twocomplementsub_4bits (
  input  A3,
  input  A2,
  input  A1,
  input  A0,
  input  B3,
  input  B2,
  input  B1,
  input  B0,
  output OVERF,
  output S3,
  output S2,
  output S1,
  output S0
);

  wire full_adder_2_cout, full_adder_3_cout, full_adder_4_cout, not_1_out, not_2_out, not_3_out, not_4_out;

  full_adder full_adder_1 (.A(A3), .B(not_1_out), .Cin(full_adder_2_cout), .S(S3), .Cout(OVERF));
  full_adder full_adder_2 (.A(A2), .B(not_2_out), .Cin(full_adder_3_cout), .S(S2), .Cout(full_adder_2_cout));
  not not_1 (not_1_out, B3);
  not not_2 (not_2_out, B2);
  not not_3 (not_3_out, B1);
  full_adder full_adder_3 (.A(A1), .B(not_3_out), .Cin(full_adder_4_cout), .S(S1), .Cout(full_adder_3_cout));
  not not_4 (not_4_out, B0);
  full_adder full_adder_4 (.A(A0), .B(not_4_out), .Cin(1'b1), .S(S0), .Cout(full_adder_4_cout));
endmodule

module full_adder (
  input  A,
  input  B,
  input  Cin,
  output S,
  output Cout
);

  wire and_1_out, and_2_out, and_3_out, xor_1_out;

  xor xor_1 (xor_1_out, A, B);
  and and_1 (and_1_out, A, B);
  and and_2 (and_2_out, A, Cin);
  and and_3 (and_3_out, B, Cin);
  xor xor_2 (S, xor_1_out, Cin);
  or or_1 (Cout, and_1_out, and_2_out, and_3_out);

  // Notes on the sheet:
  //   S = (A ⊕ B) ⊕ Cin
  //   Cout = (A . B) + (A . Cin) + (B . Cin)
endmodule

module full_subtractor (
  input  A,
  input  B,
  input  Cin,
  output S,
  output Cout
);

  wire and_1_out, and_2_out, and_3_out, not_1_out, xor_1_out;

  not not_1 (not_1_out, A);
  xor xor_1 (xor_1_out, A, B);
  and and_1 (and_1_out, not_1_out, B);
  and and_2 (and_2_out, not_1_out, Cin);
  and and_3 (and_3_out, B, Cin);
  xor xor_2 (S, xor_1_out, Cin);
  or or_1 (Cout, and_1_out, and_2_out, and_3_out);

  // Notes on the sheet:
  //   S = (A ⊕ B) ⊕ Cin
  //   Cout = (A' . B) + (A' . Cin) + (B . Cin)
endmodule

module or_vet (
  input  [4:0] A,
  input  [4:0] B,
  output [4:0] S
);

  or S4 (S[4], B[4], A[4]);
  or S3 (S[3], B[3], A[3]);
  or S2 (S[2], B[2], A[2]);
  or S1 (S[1], B[1], A[1]);
  or S0 (S[0], A[0], B[0]);
endmodule
